# Fritzing sketch schemaElettrico (saved by Fritzing 1.0.5)
breadboards: 1

parts:
  Componente1 = Arduino Uno (Rev3)
  LED1 = smd LED [color="Green (560nm)" package="0805 [SMD]"]
  LED3 = smd LED [color="Yellow (592nm)" package="0805 [SMD]"]
  LED4 = smd LED [color="Red (633nm)" package="0805 [SMD]"]
  LED5 = smd LED [color="Green (560nm)" package="0805 [SMD]"]
  LED6 = smd LED [color="Yellow (592nm)" package="0805 [SMD]"]
  LED7 = smd LED [color="Red (633nm)" package="0805 [SMD]"]
  LED8 = smd LED [color="Green (560nm)" package="0805 [SMD]"]
  LED9 = smd LED [color="Yellow (592nm)" package="0805 [SMD]"]
  LED10 = smd LED [color="Red (633nm)" package="0805 [SMD]"]
  R1 = Resistor [tolerance=±5% power=0.25W resistance=220 package=THT]
  R2 = Resistor [tolerance=±5% power=0.25W resistance=220 package=THT]
  R3 = Resistor [tolerance=±5% power=0.25W resistance=220 package=THT]
  R4 = Resistor [tolerance=±5% power=0.25W resistance=220 package=THT]
  R5 = Resistor [tolerance=±5% power=0.25W resistance=220 package=THT]
  R6 = Resistor [tolerance=±5% power=0.25W resistance=220 package=THT]
  R7 = Resistor [tolerance=±5% power=0.25W resistance=220 package=THT]
  R8 = Resistor [tolerance=±5% power=0.25W resistance=220 package=THT]
  R9 = Resistor [tolerance=±5% power=0.25W resistance=220 package=THT]
  S1 = Pushbutton [package="[THT]"]

nets:
  N1: Componente1.D8, R7.Pin_0
  N2: Componente1.D9_PWM, R8.Pin_0
  N3: Componente1.D10_PWM/SS, R9.Pin_0
  N4: Componente1.D12/MISO, S1.Pin_3, S1.Pin_4
  N5: Componente1.GND, LED1.cathode, LED3.cathode, LED4.cathode, LED5.cathode, LED6.cathode, LED7.cathode, LED8.cathode, LED9.cathode, LED10.cathode, S1.Pin_1, S1.Pin_2
  N6: Componente1.D2, R1.Pin_0
  N7: Componente1.D3_PWM, R2.Pin_0
  N8: Componente1.D4, R3.Pin_0
  N9: Componente1.D5_PWM, R4.Pin_0
  N10: Componente1.D6_PWM, R5.Pin_0
  N11: Componente1.D7, R6.Pin_0
  N12: LED1.anode, R9.Pin_1
  N13: LED3.anode, R8.Pin_1
  N14: LED4.anode, R7.Pin_1
  N15: LED5.anode, R6.Pin_1
  N16: LED6.anode, R5.Pin_1
  N17: LED7.anode, R4.Pin_1
  N18: LED8.anode, R3.Pin_1
  N19: LED9.anode, R2.Pin_1
  N20: LED10.anode, R1.Pin_1
